# Fritzing sketch BatteryOnly (saved by Fritzing 0.9.3b)

parts:
  Teensy_3_1 = Teensy 3.2
  BAT1 = Battery Holders [package=battcom_20mm_pth]

nets:
  N1: Teensy_3_1.VBat, BAT1.+
  N2: Teensy_3_1.GND, BAT1.-

custom parts:
  Teensy 3.2: The Teensy is a complete USB-based microcontoller development system, in a very small footprint, capable of implementing many types of projects. All programming is done via the USB port. No special programmer is needed, only a standard micro-USB cable and a PC or Macintosh with a USB port. It has a USB keyboard/mouse/joystick emulation stack and can be programmed through Arduino IDE.
