# Fritzing sketch GPSOnly (saved by Fritzing 0.9.3b)

parts:
  Teensy_3_1 = Teensy 3.2
  U1 = SUP500F [package=sup500f]

nets:
  GND: Teensy_3_1.GND, U1.GND
  N1: Teensy_3_1.D0, U1.TX-O
  N2: Teensy_3_1.D1, U1.RX-I
  VIN: Teensy_3_1.Vin, U1.VCC

custom parts:
  Teensy 3.2: The Teensy is a complete USB-based microcontoller development system, in a very small footprint, capable of implementing many types of projects. All programming is done via the USB port. No special programmer is needed, only a standard micro-USB cable and a PC or Macintosh with a USB port. It has a USB keyboard/mouse/joystick emulation stack and can be programmed through Arduino IDE.
