# Fritzing sketch IMUOnly (saved by Fritzing 0.9.3b)

parts:
  Teensy_3_1 = Teensy 3.2
  R3 = 10 kΩ Resistor [package=THT]
  R2 = 10 kΩ Resistor [package=THT]
  MPU9250_MPU-1 = SparkFun IMU Breakout - MPU-9250 [part_number=" SEN-13762"]

nets:
  GND: Teensy_3_1.GND, MPU9250_MPU-1.GND
  N1: Teensy_3_1.A4/D18, R3.Pin_1, MPU9250_MPU-1.SDA/SDI
  N2: Teensy_3_1.A5/D19, R2.Pin_1, MPU9250_MPU-1.SCL/SCLK
  3V3: Teensy_3_1.3V3, R3.Pin_0, R2.Pin_0, MPU9250_MPU-1.VDD

custom parts:
  Teensy 3.2: The Teensy is a complete USB-based microcontoller development system, in a very small footprint, capable of implementing many types of projects. All programming is done via the USB port. No special programmer is needed, only a standard micro-USB cable and a PC or Macintosh with a USB port. It has a USB keyboard/mouse/joystick emulation stack and can be programmed through Arduino IDE.
  10 kΩ Resistor: A generic resistor (0.25W)
