# Fritzing sketch StarPointer (saved by Fritzing 0.9.3b)

parts:
  Teensy_3_1 = Teensy 3.2
  MPU9250_MPU-1 = SparkFun IMU Breakout - MPU-9250 [part_number=" SEN-13762"]
  BAT1 = Battery Holders [package=battcom_20mm_pth]
  U1 = SUP500F [package=sup500f]
  R3 = 10 kΩ Resistor [package=THT]
  R2 = 10 kΩ Resistor [package=THT]

nets:
  GND: Teensy_3_1.GND, MPU9250_MPU-1.GND, BAT1.-, U1.GND
  N1: Teensy_3_1.D0, U1.TX-O
  N2: Teensy_3_1.D1, U1.RX-I
  N3: Teensy_3_1.VBat, BAT1.+
  N4: Teensy_3_1.A4/D18, MPU9250_MPU-1.SDA/SDI, R3.Pin_1
  N5: Teensy_3_1.A5/D19, MPU9250_MPU-1.SCL/SCLK, R2.Pin_1
  3V3: Teensy_3_1.3V3, MPU9250_MPU-1.VDD, R3.Pin_0, R2.Pin_0
  VIN: Teensy_3_1.Vin, U1.VCC

custom parts:
  Teensy 3.2: The Teensy is a complete USB-based microcontoller development system, in a very small footprint, capable of implementing many types of projects. All programming is done via the USB port. No special programmer is needed, only a standard micro-USB cable and a PC or Macintosh with a USB port. It has a USB keyboard/mouse/joystick emulation stack and can be programmed through Arduino IDE.
  10 kΩ Resistor: A generic resistor (0.25W)
